# Fritzing sketch sketch (saved by Fritzing 0.9.3b)
breadboards: 1

parts:
  Raspberry_Pi_1 = Raspberry Pi 3 [part_number=RPI-3-V1.2]
  LED1 = LED - 5mm [color="Red (633nm)" package="5 mm [THT]"]
  LED2 = LED - 5mm [color="Blue (525nm)" package="5 mm [THT]"]
  ADC0832 = IC, DIP package, 8 pins [chip_label=ADC0832]
  LED3 = LED - 5mm [color="Green (555nm)" package="5 mm [THT]"]
  R1 = Resistor [tolerance=±5% resistance=220 package=THT]
  R2 = Resistor [tolerance=±5% resistance=220 package=THT]
  R3 = Resistor [tolerance=±5% resistance=220 package=THT]
  Water_Level_Sensor1 = Water Level Sensor

nets:
  3V3: Raspberry_Pi_1.3v3, Raspberry_Pi_1.GPIO2, Raspberry_Pi_1.GPIO22, Raspberry_Pi_1.3V3, Raspberry_Pi_1.GPIO10, ADC0832.pin8, Water_Level_Sensor1.VCC
  GND: Raspberry_Pi_1.GPIO4, Raspberry_Pi_1.GND, Raspberry_Pi_1.GPIO12, Raspberry_Pi_1.GPIO23, Raspberry_Pi_1.GPIO18, ADC0832.pin4, R1.Pin_0, R2.Pin_0, R3.Pin_0, Water_Level_Sensor1.GND
  N1: Raspberry_Pi_1.GPIO17, Raspberry_Pi_1.GPIO27, ADC0832.pin1
  N2: Raspberry_Pi_1.ID_SD, Raspberry_Pi_1.GPIO5, LED3.anode
  N3: Raspberry_Pi_1.GPIO6, Raspberry_Pi_1.GPIO13, LED2.anode
  N4: Raspberry_Pi_1.GPIO19, Raspberry_Pi_1.GPIO26, LED1.anode
  N5: Raspberry_Pi_1.GPIO21, ADC0832.pin5
  N6: Raspberry_Pi_1.GPIO20, ADC0832.pin6
  N7: Raspberry_Pi_1.GPIO16, ADC0832.pin7
  N8: LED1.cathode, R3.Pin_1
  N9: LED2.cathode, R2.Pin_1
  N10: ADC0832.pin2, Water_Level_Sensor1.SIG
  N11: LED3.cathode, R1.Pin_1

custom parts:
  Water Level Sensor: A water level sensor. This sensor operates at 3V to 5V. The Sig (signal) pin outputs an analogue signal that is in proportion to the amount of water in contact with the sensor.
